# Fritzing sketch Krugers's Diagram (saved by Fritzing 0.9.3b)
breadboards: 1

parts:
  R1 = Resistor [tolerance=±5% resistance=4.7k package=THT]
  R2 = Temperature Sensor (Thermistor) [thermistor_type=NTC package=THT]
  R3 = PHOTOCELL [package=photocell]
  R4 = Resistor [tolerance=±5% resistance=220 package=THT]

nets:
  N1: R1.Pin_1, R2.pin_0
  N2: R3.P$1, R4.Pin_1
