# Fritzing sketch DigitalCircuitModel (saved by Fritzing 0.9.3b)
breadboards: 1

parts:
  Part1 = Arduino Due (Rev2b)
  J1 = Piezo Speaker

nets:
  N1: Part1.D12_PWM, J1.pin2
  N2: Part1.GND, J1.pin1
